// Logisim project Multiplication.circ as structural Verilog: 3 circuits, main circuit main
module main (
  input  A2,
  input  A1,
  input  A0,
  input  B2,
  input  B1,
  input  B0,
  output S1,
  output S2,
  output S3,
  output S4,
  output S5,
  output out_12
);

  Multiplier_with_signs multiplier_with_signs_1 (
    .A2(A2), .A1(A1), .A0(A0), .B2(B2), .B1(B1), .B0(B0), .S1(S1), .S2(S2), .S3(S3), .S4(S4), .S5(S5),
    .out_12(out_12));

  // Notes on the sheet:
  //   sign flag
endmodule

module Half_adder (
  input  X,
  input  in_2,
  output Sum,
  output Carry
);

  xor xor_1 (Sum, X, in_2);
  and and_1 (Carry, X, in_2);
endmodule

module Multiplier_with_signs (
  input  A2,
  input  A1,
  input  A0,
  input  B2,
  input  B1,
  input  B0,
  output S1,
  output S2,
  output S3,
  output S4,
  output S5,
  output out_12
);

  wire and_2_out, and_3_out, and_4_out, half_adder_1_carry;

  and and_1 (S1, B0, A0);
  and and_2 (and_2_out, A0, B1);
  and and_3 (and_3_out, B0, A1);
  and and_4 (and_4_out, B1, A1);
  xor xor_1 (out_12, A2, B2);
  Half_adder half_adder_1 (.X(and_2_out), .in_2(and_3_out), .Sum(S2), .Carry(half_adder_1_carry));
  Half_adder half_adder_2 (.X(half_adder_1_carry), .in_2(and_4_out), .Sum(S3), .Carry(S4));

  assign S5 = out_12;

  // Notes on the sheet:
  //   sign flag
endmodule
